// Logisim project 2_bit_adder.circ as structural Verilog: 1 circuit, main circuit main
module main (
  input  in_1,
  input  in_2,
  input  in_3,
  input  in_4,
  input  in_5,
  output out_6,
  output out_7,
  output out_8
);

  wire full_adder_2_out_5;

  half_adder full_adder (.in_1(in_3), .in_2(in_1), .carry_in(full_adder_2_out_5), .out_5(out_6), .out_4(out_7));
  half_adder full_adder_2 (.in_1(in_4), .in_2(in_2), .carry_in(in_5), .out_5(full_adder_2_out_5), .out_4(out_8));
endmodule
