// Logisim project 4_bit_adder.circ as structural Verilog: 1 circuit, main circuit main
module main (
  input  in_1,
  input  in_2,
  input  in_3,
  input  in_4,
  input  in_5,
  input  in_6,
  input  in_7,
  input  in_8,
  input  in_9,
  output out_10,
  output out_11,
  output out_12,
  output out_13,
  output out_14
);

  wire main_2_out_6;

  _2_bit_adder_main main_1 (
    .out_6(out_10), .in_1(in_1), .in_2(in_2), .in_3(in_3), .in_4(in_4), .out_7(out_11), .out_8(out_12),
    .in_5(main_2_out_6));
  _2_bit_adder_main main_2 (
    .out_6(main_2_out_6), .in_1(in_5), .in_2(in_6), .in_3(in_7), .in_4(in_8), .out_7(out_13), .out_8(out_14),
    .in_5(in_9));
endmodule
