// Logisim project full_adder.circ as structural Verilog
module half_adder (
  input  in_1,
  input  in_2,
  input  carry_in,
  output out_4,
  output out_5
);

  wire main_1_out_3, main_1_out_4, main_2_out_3;

  half_adder_main main_1 (.in_1(in_1), .in_2(in_2), .out_3(main_1_out_3), .out_4(main_1_out_4));
  or or_1 (out_5, main_1_out_3, main_2_out_3);
  half_adder_main main_2 (.in_1(main_1_out_4), .in_2(carry_in), .out_3(main_2_out_3), .out_4(out_4));
endmodule
